# Fritzing sketch circuit-assembly (saved by Fritzing 0.9.5d)

parts:
  Arduino_UNO_R3_-_USB = Arduino Uno (Rev3) - ICSP
  DFPlayer_Mini_+_microSD = DFRobot DFPlayer Mini [part_number=DFR0299]
  modul_Bluetooth = Bluetooth HC-06
  Difuzor_2_W_/_8_Ohm = Loudspeaker
  R1_-_1_kOhm = Resistor [resistance=1k package=THT]
  R2_-_1_kOhm = Resistor [resistance=1k package=THT]
  R3_-_2_kOhm = Resistor [resistance=2k package=THT]
  OLED_0_96_I2C = OLED 0.96" 128x64 I2C SSD1306 (GND/VCC)
  Modul_8_Butoane = SIO_Keypad8_Header8_GND_20261101_v4
  Sursa_5_V = SIO_Power5V_20261101_v2

nets:
  N1: Arduino_UNO_R3_-_USB.A0, modul_Bluetooth.TXD
  N2: Arduino_UNO_R3_-_USB.A4/SDA, OLED_0_96_I2C.SCA
  N3: Arduino_UNO_R3_-_USB.A5/SCL, OLED_0_96_I2C.SCL
  N4: Arduino_UNO_R3_-_USB.D8, Modul_8_Butoane.connector6
  N5: Arduino_UNO_R3_-_USB.D9_PWM, Modul_8_Butoane.connector7
  N6: Arduino_UNO_R3_-_USB.D10_PWM/SS, R2_-_1_kOhm.Pin_0
  N7: Arduino_UNO_R3_-_USB.D11_PWM/MOSI, R1_-_1_kOhm.Pin_0
  N8: Arduino_UNO_R3_-_USB.D12/MISO, DFPlayer_Mini_+_microSD.BUSY
  N9: Arduino_UNO_R3_-_USB.D2, Modul_8_Butoane.connector0
  N10: Arduino_UNO_R3_-_USB.D3_PWM, Modul_8_Butoane.connector1
  N11: Arduino_UNO_R3_-_USB.D4, Modul_8_Butoane.connector2
  N12: Arduino_UNO_R3_-_USB.D5_PWM, Modul_8_Butoane.connector3
  N13: Arduino_UNO_R3_-_USB.D6_PWM, Modul_8_Butoane.connector4
  N14: Arduino_UNO_R3_-_USB.D7, Modul_8_Butoane.connector5
  GND: Arduino_UNO_R3_-_USB.GND, DFPlayer_Mini_+_microSD.GND-1, modul_Bluetooth.GND, R3_-_2_kOhm.Pin_1, OLED_0_96_I2C.GND, Modul_8_Butoane.connector8, Sursa_5_V.connector1
  VCC: DFPlayer_Mini_+_microSD.VCC, modul_Bluetooth.VCC, OLED_0_96_I2C.VCC, Sursa_5_V.connector0
  N15: DFPlayer_Mini_+_microSD.RX, R1_-_1_kOhm.Pin_1
  N16: DFPlayer_Mini_+_microSD.SPK_1, Difuzor_2_W_/_8_Ohm.pin1
  N17: DFPlayer_Mini_+_microSD.SPK_2, Difuzor_2_W_/_8_Ohm.pin2
  N18: modul_Bluetooth.RXD, R2_-_1_kOhm.Pin_1, R3_-_2_kOhm.Pin_0

custom parts:
  220 Ω Resistor: A generic resistor (0.25W)
  220 Ω Resistor: A generic resistor (0.25W)
  OLED 0.96" 128x64 I2C SSD1306 (GND/VCC): OLED 0.96" 128x64 I2C SSD1306 Pinout: GND/VCC/SCL/SDA
